// Logisim project main.circ as structural Verilog: 5 circuits, main circuit main
module main (
  input  Hold
);

  wire \bit , but_control_1_irq, cdm16e_1_p3, cdm16e_1_p5, cdm16e_1_p8, cdm16e_1_p9, cdm16e_1_p10,
       cdm16e_1_p11, cdm16e_1_p12, cdm16e_1_p13, cdm16e_1_p14, cdm16e_1_p15, cdm16e_1_p16, cl,
       comparator_1_eq, down, ld, left, life_off, life_on, mem, not_1_out, not_2_out, read, reset_all, right,
       screen_control_1_clock_out, screen_control_2_clock_out, screen_control_3_clock_out,
       screen_control_4_clock_out, set, up;
  wire [2:1] CR3IN, CR3OUT, CR4IN, CR4OUT, CR5IN, CR5OUT, CR6IN, CR6OUT;
  wire [3:0] CR1IN, CR1OUT, CR2IN, CR2OUT;
  wire [5:0] but_control_1_vec;
  wire [15:0] addr, cdm16e_1_p21, cdm16e_1_p22, data, L1left, L1right, L2left, L2right, L3left, L3right,
       L4left, L4right, np1, np2, np3, r1, S1NG0, S1NG1, S1NG2, S1NG3, S1NG4, S1NG5, S1NG6, S1NG7, S1NG8,
       S1NG9, S1NG10, S1NG11, S1NG12, S1NG13, S1NG14, S1NG15, S1NG16, S1NG17, S1NG18, S1NG19, S1NG20, S1NG21,
       S1NG22, S1NG23, S1NG24, S1NG25, S1NG26, S1NG27, S1NG28, S1NG29, S1NG30, S1NG31,
       screen_control_1_addr_pass, screen_control_1_data_pass, screen_control_1_next_pos,
       screen_control_1_str_left_out, screen_control_1_str_right_out, screen_control_2_addr_pass,
       screen_control_2_data_pass, screen_control_2_next_pos, screen_control_2_str_left_out,
       screen_control_2_str_right_out, screen_control_3_addr_pass, screen_control_3_data_pass,
       screen_control_3_next_pos, screen_control_3_str_left_out, screen_control_3_str_right_out,
       screen_control_4_addr_pass, screen_control_4_data_pass, screen_control_4_next_pos,
       screen_control_4_str_left_out, screen_control_4_str_right_out;
  wire [31:0] C1DU1_2, C1DU2_3, C1DU3_4, C1DU4_1, C1UD1_4, C1UD2_1, C1UD3_2, C1UD4_3, C2DU1_2, C2DU2_3,
       C2DU3_4, C2DU4_1, C2UD1_4, C2UD2_1, C2UD3_2, C2UD4_3;

  // Probe on cdm16e_1_p5
  // Probe on cdm16e_1_p5
  // Probe on cdm16e_1_p5
  DotMatrix #(.matrixcols(32), .matrixrows(16)) dotmatrix_1 (
    .col0(S1NG0), .col1(S1NG1), .col2(S1NG2), .col3(S1NG3), .col4(S1NG4), .col5(S1NG5), .col6(S1NG6),
    .col7(S1NG7), .col8(S1NG8), .col9(S1NG9), .col10(S1NG10), .col11(S1NG11), .col12(S1NG12), .col13(S1NG13),
    .col14(S1NG14), .col15(S1NG15), .col16(S1NG16), .col17(S1NG17), .col18(S1NG18), .col19(S1NG19),
    .col20(S1NG20), .col21(S1NG21), .col22(S1NG22), .col23(S1NG23), .col24(S1NG24), .col25(S1NG25),
    .col26(S1NG26), .col27(S1NG27), .col28(S1NG28), .col29(S1NG29), .col30(S1NG30), .col31(S1NG31));
  // Probe on cdm16e_1_p5
  // Probe on r1
  // Probe on r1
  // Probe on r1
  but_control but_control_1 (
    .set_op(set), .IRQ(but_control_1_irq), .IAck(cdm16e_1_p3), .down(down), .left(left), .right(right),
    .up(up), .clock(cl), .reset_all(reset_all), .life_on(life_on), .data(data), .addr(addr), .read(read),
    .vec(but_control_1_vec), .life_off(life_off));
  Clock clock_1 (.out(cl));
  // Probe on cdm16e_1_p8
  // Probe on cdm16e_1_p8
  // Probe on cdm16e_1_p8
  // cdm16e cdm16e_1: pin names not known; wires that end beside it: but_control_1_irq, but_control_1_vec, cdm16e_1_p3, Hold, cdm16e_1_p5, r1, cl, cdm16e_1_p8, cdm16e_1_p9, cdm16e_1_p10, cdm16e_1_p11, cdm16e_1_p12, cdm16e_1_p13, cdm16e_1_p14, cdm16e_1_p15, cdm16e_1_p16, mem, read, \bit , addr, cdm16e_1_p21, cdm16e_1_p22
  Button v (.out(life_on));
  Button u_u (.out(life_off));
  Button _0_o (.out(reset_all));
  // Probe on cdm16e_1_p9
  // Probe on cdm16e_1_p9
  // Probe on cdm16e_1_p9
  not not_1 (not_1_out, read);
  assign cdm16e_1_p22 = read ? data : 16'bz;  // Controlled_Buffer controlled_buffer_1
  Button button (.out(up));
  Button button_2 (.out(left));
  Button v_2 (.out(down));
  Button u_set (.out(set));
  // Probe on cdm16e_1_p10
  // Probe on cdm16e_1_p10
  // Probe on cdm16e_1_p10
  assign data = not_1_out ? cdm16e_1_p21 : 16'bz;  // Controlled_Buffer controlled_buffer_2
  Button button_3 (.out(right));
  // Probe on cdm16e_1_p11
  // Probe on cdm16e_1_p11
  // Probe on cdm16e_1_p11
  // Probe on data
  // Probe on data
  // Probe on data
  // Probe on data
  // Probe on cdm16e_1_p12
  // Probe on cdm16e_1_p12
  // Probe on cdm16e_1_p12
  // Probe on addr
  // Probe on addr
  // Probe on addr
  // Probe on addr
  // Probe on cdm16e_1_p13
  // Probe on cdm16e_1_p13
  // Probe on cdm16e_1_p13
  // RAM ram_1: pin names not known; wires that end beside it: addr, \bit , mem, cl, ld, data
  screen_control screen_control_1 (
    .clock(cl), .data(data), .addr(addr), .start_pos(r1), .next_pos(screen_control_1_next_pos),
    .clock_out(screen_control_1_clock_out), .data_pass(screen_control_1_data_pass),
    .addr_pass(screen_control_1_addr_pass), .str_up_out(C1UD1_4), .str_down_out(C1DU1_2),
    .str_up_in(C1DU4_1), .str_down_in(C1UD2_1), .str_right_out(screen_control_1_str_right_out),
    .str_left_out(screen_control_1_str_left_out), .str_right_in(L1right), .str_left_in(L1left),
    .corners_in(CR1IN), .corners_out(CR1OUT), .next_gen_0(S1NG0), .next_gen_1(S1NG1), .next_gen_2(S1NG2),
    .next_gen_3(S1NG3), .next_gen_4(S1NG4), .next_gen_5(S1NG5), .next_gen_6(S1NG6), .next_gen_7(S1NG7),
    .next_gen_8(S1NG8), .next_gen_9(S1NG9), .next_gen_10(S1NG10), .next_gen_11(S1NG11), .next_gen_12(S1NG12),
    .next_gen_13(S1NG13), .next_gen_14(S1NG14), .next_gen_15(S1NG15), .next_gen_16(S1NG16),
    .next_gen_17(S1NG17), .next_gen_18(S1NG18), .next_gen_19(S1NG19), .next_gen_20(S1NG20),
    .next_gen_21(S1NG21), .next_gen_22(S1NG22), .next_gen_23(S1NG23), .next_gen_24(S1NG24),
    .next_gen_25(S1NG25), .next_gen_26(S1NG26), .next_gen_27(S1NG27), .next_gen_28(S1NG28),
    .next_gen_29(S1NG29), .next_gen_30(S1NG30), .next_gen_31(S1NG31));  // open: str16, str17, str18, str19, str20, str21, str22, str23, str24, str25, str26, str27, str28, str29, str30, str31, str0, str1, str2, str3, str4, str5, str6, str7, str8, str9, str10, str11, str12, str13, str14, str15
  screen_control screen_control_2 (
    .clock(cl), .data(data), .addr(addr), .start_pos(np1), .next_pos(screen_control_2_next_pos),
    .clock_out(screen_control_2_clock_out), .data_pass(screen_control_2_data_pass),
    .addr_pass(screen_control_2_addr_pass), .str_up_out(C1UD2_1), .str_down_out(C1DU2_3),
    .str_up_in(C1DU1_2), .str_down_in(C1UD3_2), .str_right_out(screen_control_2_str_right_out),
    .str_left_out(screen_control_2_str_left_out), .str_right_in(L2right), .str_left_in(L2left),
    .corners_in({CR2OUT[1], CR3IN, CR2OUT[2]}), .corners_out({CR2IN[1], CR3OUT, CR2IN[2]}));  // open: next_gen_0, next_gen_1, next_gen_2, next_gen_3, next_gen_4, next_gen_5, next_gen_6, next_gen_7, next_gen_8, next_gen_9, next_gen_10, next_gen_11, next_gen_12, next_gen_13, next_gen_14, next_gen_15, next_gen_16, next_gen_17, next_gen_18, next_gen_19, next_gen_20, next_gen_21, next_gen_22, next_gen_23, next_gen_24, next_gen_25, next_gen_26, next_gen_27, next_gen_28, next_gen_29, next_gen_30, next_gen_31, str16, str17, str18, str19, str20, str21, str22, str23, str24, str25, str26, str27, str28, str29, str30, str31, str0, str1, str2, str3, str4, str5, str6, str7, str8, str9, str10, str11, str12, str13, str14, str15
  screen_control screen_control_3 (
    .clock(cl), .data(data), .addr(addr), .start_pos(np2), .next_pos(screen_control_3_next_pos),
    .clock_out(screen_control_3_clock_out), .data_pass(screen_control_3_data_pass),
    .addr_pass(screen_control_3_addr_pass), .str_up_out(C1UD3_2), .str_down_out(C1DU3_4),
    .str_up_in(C1DU2_3), .str_down_in(C1UD4_3), .str_right_out(screen_control_3_str_right_out),
    .str_left_out(screen_control_3_str_left_out), .str_right_in(L3right), .str_left_in(L3left),
    .corners_in({CR4OUT[1], CR5IN, CR4OUT[2]}), .corners_out({CR4IN[1], CR5OUT, CR4IN[2]}));  // open: next_gen_0, next_gen_1, next_gen_2, next_gen_3, next_gen_4, next_gen_5, next_gen_6, next_gen_7, next_gen_8, next_gen_9, next_gen_10, next_gen_11, next_gen_12, next_gen_13, next_gen_14, next_gen_15, next_gen_16, next_gen_17, next_gen_18, next_gen_19, next_gen_20, next_gen_21, next_gen_22, next_gen_23, next_gen_24, next_gen_25, next_gen_26, next_gen_27, next_gen_28, next_gen_29, next_gen_30, next_gen_31, str16, str17, str18, str19, str20, str21, str22, str23, str24, str25, str26, str27, str28, str29, str30, str31, str0, str1, str2, str3, str4, str5, str6, str7, str8, str9, str10, str11, str12, str13, str14, str15
  screen_control screen_control_4 (
    .clock(cl), .data(data), .addr(addr), .start_pos(np3), .next_pos(screen_control_4_next_pos),
    .clock_out(screen_control_4_clock_out), .data_pass(screen_control_4_data_pass),
    .addr_pass(screen_control_4_addr_pass), .str_up_out(C1UD4_3), .str_down_out(C1DU4_1),
    .str_up_in(C1DU3_4), .str_down_in(C1UD1_4), .str_right_out(screen_control_4_str_right_out),
    .str_left_out(screen_control_4_str_left_out), .str_right_in(L4right), .str_left_in(L4left),
    .corners_in({CR6OUT[1], CR2OUT[0], CR2OUT[3], CR6OUT[2]}),
    .corners_out({CR6IN[1], CR2IN[0], CR2IN[3], CR6IN[2]}));  // open: next_gen_0, next_gen_1, next_gen_2, next_gen_3, next_gen_4, next_gen_5, next_gen_6, next_gen_7, next_gen_8, next_gen_9, next_gen_10, next_gen_11, next_gen_12, next_gen_13, next_gen_14, next_gen_15, next_gen_16, next_gen_17, next_gen_18, next_gen_19, next_gen_20, next_gen_21, next_gen_22, next_gen_23, next_gen_24, next_gen_25, next_gen_26, next_gen_27, next_gen_28, next_gen_29, next_gen_30, next_gen_31, str16, str17, str18, str19, str20, str21, str22, str23, str24, str25, str26, str27, str28, str29, str30, str31, str0, str1, str2, str3, str4, str5, str6, str7, str8, str9, str10, str11, str12, str13, str14, str15
  // Probe on cdm16e_1_p14
  // Probe on cdm16e_1_p14
  // Probe on cdm16e_1_p14
  // Debugger debugger_1: pin names not known
  // Probe on cdm16e_1_p15
  // Probe on cdm16e_1_p15
  // Probe on cdm16e_1_p15
  and and_1 (ld, read, not_2_out);
  not not_2 (not_2_out, comparator_1_eq);
  Comparator #(.width(16)) comparator_1 (.a(addr), .b(16'hfff0), .eq(comparator_1_eq));  // open: gt, lt
  // Probe on cdm16e_1_p16
  // Probe on cdm16e_1_p16
  // Probe on cdm16e_1_p16
  // Probe on cdm16e_1_p16
  screen_control screen_control_5 (
    .clock(screen_control_1_clock_out), .data(screen_control_1_data_pass), .addr(screen_control_1_addr_pass),
    .start_pos(screen_control_1_next_pos), .next_pos(np1), .str_up_out(C2UD1_4), .str_down_out(C2DU1_2),
    .str_up_in(C2DU4_1), .str_down_in(C2UD2_1), .str_right_out(L1left), .str_left_out(L1right),
    .str_right_in(screen_control_1_str_left_out), .str_left_in(screen_control_1_str_right_out),
    .corners_in(CR2IN), .corners_out(CR2OUT));  // open: clock_out, data_pass, addr_pass, next_gen_0, next_gen_1, next_gen_2, next_gen_3, next_gen_4, next_gen_5, next_gen_6, next_gen_7, next_gen_8, next_gen_9, next_gen_10, next_gen_11, next_gen_12, next_gen_13, next_gen_14, next_gen_15, next_gen_16, next_gen_17, next_gen_18, next_gen_19, next_gen_20, next_gen_21, next_gen_22, next_gen_23, next_gen_24, next_gen_25, next_gen_26, next_gen_27, next_gen_28, next_gen_29, next_gen_30, next_gen_31, str16, str17, str18, str19, str20, str21, str22, str23, str24, str25, str26, str27, str28, str29, str30, str31, str0, str1, str2, str3, str4, str5, str6, str7, str8, str9, str10, str11, str12, str13, str14, str15
  screen_control screen_control_6 (
    .clock(screen_control_2_clock_out), .data(screen_control_2_data_pass), .addr(screen_control_2_addr_pass),
    .start_pos(screen_control_2_next_pos), .next_pos(np2), .str_up_out(C2UD2_1), .str_down_out(C2DU2_3),
    .str_up_in(C2DU1_2), .str_down_in(C2UD3_2), .str_right_out(L2left), .str_left_out(L2right),
    .str_right_in(screen_control_2_str_left_out), .str_left_in(screen_control_2_str_right_out),
    .corners_in({CR1OUT[1], CR4IN, CR1OUT[2]}), .corners_out({CR1IN[1], CR4OUT, CR1IN[2]}));  // open: clock_out, data_pass, addr_pass, next_gen_0, next_gen_1, next_gen_2, next_gen_3, next_gen_4, next_gen_5, next_gen_6, next_gen_7, next_gen_8, next_gen_9, next_gen_10, next_gen_11, next_gen_12, next_gen_13, next_gen_14, next_gen_15, next_gen_16, next_gen_17, next_gen_18, next_gen_19, next_gen_20, next_gen_21, next_gen_22, next_gen_23, next_gen_24, next_gen_25, next_gen_26, next_gen_27, next_gen_28, next_gen_29, next_gen_30, next_gen_31, str16, str17, str18, str19, str20, str21, str22, str23, str24, str25, str26, str27, str28, str29, str30, str31, str0, str1, str2, str3, str4, str5, str6, str7, str8, str9, str10, str11, str12, str13, str14, str15
  screen_control screen_control_7 (
    .clock(screen_control_3_clock_out), .data(screen_control_3_data_pass), .addr(screen_control_3_addr_pass),
    .start_pos(screen_control_3_next_pos), .next_pos(np3), .str_up_out(C2UD3_2), .str_down_out(C2DU3_4),
    .str_up_in(C2DU2_3), .str_down_in(C2UD4_3), .str_right_out(L3left), .str_left_out(L3right),
    .str_right_in(screen_control_3_str_left_out), .str_left_in(screen_control_3_str_right_out),
    .corners_in({CR3OUT[1], CR6IN, CR3OUT[2]}), .corners_out({CR3IN[1], CR6OUT, CR3IN[2]}));  // open: clock_out, data_pass, addr_pass, next_gen_0, next_gen_1, next_gen_2, next_gen_3, next_gen_4, next_gen_5, next_gen_6, next_gen_7, next_gen_8, next_gen_9, next_gen_10, next_gen_11, next_gen_12, next_gen_13, next_gen_14, next_gen_15, next_gen_16, next_gen_17, next_gen_18, next_gen_19, next_gen_20, next_gen_21, next_gen_22, next_gen_23, next_gen_24, next_gen_25, next_gen_26, next_gen_27, next_gen_28, next_gen_29, next_gen_30, next_gen_31, str16, str17, str18, str19, str20, str21, str22, str23, str24, str25, str26, str27, str28, str29, str30, str31, str0, str1, str2, str3, str4, str5, str6, str7, str8, str9, str10, str11, str12, str13, str14, str15
  screen_control screen_control_8 (
    .clock(screen_control_4_clock_out), .data(screen_control_4_data_pass), .addr(screen_control_4_addr_pass),
    .start_pos(screen_control_4_next_pos), .str_up_out(C2UD4_3), .str_down_out(C2DU4_1), .str_up_in(C2DU3_4),
    .str_down_in(C2UD1_4), .str_right_out(L4left), .str_left_out(L4right),
    .str_right_in(screen_control_4_str_left_out), .str_left_in(screen_control_4_str_right_out),
    .corners_in({CR5OUT[1], CR1OUT[0], CR1OUT[3], CR5OUT[2]}),
    .corners_out({CR5IN[1], CR1IN[0], CR1IN[3], CR5IN[2]}));  // open: next_pos, clock_out, data_pass, addr_pass, next_gen_0, next_gen_1, next_gen_2, next_gen_3, next_gen_4, next_gen_5, next_gen_6, next_gen_7, next_gen_8, next_gen_9, next_gen_10, next_gen_11, next_gen_12, next_gen_13, next_gen_14, next_gen_15, next_gen_16, next_gen_17, next_gen_18, next_gen_19, next_gen_20, next_gen_21, next_gen_22, next_gen_23, next_gen_24, next_gen_25, next_gen_26, next_gen_27, next_gen_28, next_gen_29, next_gen_30, next_gen_31, str16, str17, str18, str19, str20, str21, str22, str23, str24, str25, str26, str27, str28, str29, str30, str31, str0, str1, str2, str3, str4, str5, str6, str7, str8, str9, str10, str11, str12, str13, str14, str15

  // Other names for the same wires on the sheet: CR7IN[3:0] = {CR6OUT[1], CR2OUT[0], CR2OUT[3], CR6OUT[2]};
  //   CR3IN (some bits) = {CR2OUT[1], CR2OUT[2]}; CR3OUT (some bits) = {CR2IN[1], CR2IN[2]};
  //   CR6IN (some bits) = {CR3OUT[1], CR3OUT[2]}; CR4IN (some bits) = {CR1OUT[1], CR1OUT[2]};
  //   CR4OUT (some bits) = {CR1IN[1], CR1IN[2]}; CR5IN (some bits) = {CR4OUT[1], CR4OUT[2]};
  //   CR5OUT (some bits) = {CR4IN[1], CR4IN[2]}; CR8IN[3:0] = {CR5OUT[1], CR1OUT[0], CR1OUT[3], CR5OUT[2]};
  //   CR6OUT (some bits) = {CR3IN[1], CR3IN[2]}; CR7OUT[3:0] = {CR6IN[1], CR2IN[0], CR2IN[3], CR6IN[2]};
  //   CR8OUT[3:0] = {CR5IN[1], CR1IN[0], CR1IN[3], CR5IN[2]}

  // Notes on the sheet:
  //   r0
  //   r1
  //   r2
  //   r3
  //   r4
  //   Pointer
  //   r5
  //   r6
  //   fp
  //   pc
  //   sp
  //   ps
endmodule

module data_sel (
  input  [15:0] out,
  input  r_w,
  input  [15:0] in,
  output [15:0] data
);

  wire not_1_out;

  assign data = not_1_out ? out : 16'bz;  // Controlled_Buffer controlled_buffer_1
  not not_1 (not_1_out, r_w);
  assign in = r_w ? data : 16'bz;  // Controlled_Buffer controlled_buffer_2
endmodule

// MEM BANK
module gpu_str_mem (
  input  [15:0] data,
  input  [15:0] addr,
  input  clock,
  input  [15:0] pos,
  output [15:0] str,
  output [15:0] pos_next
);

  wire comparator_1_eq;
  wire [15:0] multiplexer_1_out;

  // Probe on pos
  Comparator #(.width(16), .mode("unsigned")) comparator_1 (.a(addr), .b(pos), .eq(comparator_1_eq));  // open: gt, lt
  Adder #(.width(16)) adder_1 (.a(pos), .b(16'h2), .out(pos_next));  // open: cin, cout
  Multiplexer #(.width(16), .enable("false")) multiplexer_1 (
    .in0(str), .in1(data), .out(multiplexer_1_out), .sel(comparator_1_eq));
  Register #(.width(16)) register_1 (.D(multiplexer_1_out), .Q(str), .clk(clock));  // open: en, clr
endmodule

// SCREEN CONTROL\nMODULE
module screen_control (
  input  [15:0] data,
  input  [15:0] addr,
  input  clock,
  input  [15:0] start_pos,
  input  [31:0] str_up_in,
  input  [31:0] str_down_in,
  input  [15:0] str_right_in,
  input  [15:0] str_left_in,
  input  [3:0] corners_in,
  output [15:0] str0,
  output [15:0] str1,
  output [15:0] str2,
  output [15:0] str3,
  output [15:0] str4,
  output [15:0] str5,
  output [15:0] str6,
  output [15:0] str7,
  output [15:0] str8,
  output [15:0] str9,
  output [15:0] str10,
  output [15:0] str11,
  output [15:0] str12,
  output [15:0] str13,
  output [15:0] str14,
  output [15:0] str15,
  output [31:0] str_down_out,
  output [31:0] str_up_out,
  output [15:0] data_pass,
  output [15:0] addr_pass,
  output clock_out,
  output [15:0] next_pos,
  output [15:0] str16,
  output [15:0] str17,
  output [15:0] str18,
  output [15:0] str19,
  output [15:0] str20,
  output [15:0] str21,
  output [15:0] str22,
  output [15:0] str23,
  output [15:0] str24,
  output [15:0] str25,
  output [15:0] str26,
  output [15:0] str27,
  output [15:0] str28,
  output [15:0] str29,
  output [15:0] str30,
  output [15:0] str31,
  output [15:0] next_gen_0,
  output [15:0] next_gen_1,
  output [15:0] next_gen_2,
  output [15:0] next_gen_3,
  output [15:0] next_gen_4,
  output [15:0] next_gen_5,
  output [15:0] next_gen_6,
  output [15:0] next_gen_7,
  output [15:0] next_gen_8,
  output [15:0] next_gen_9,
  output [15:0] next_gen_10,
  output [15:0] next_gen_11,
  output [15:0] next_gen_12,
  output [15:0] next_gen_13,
  output [15:0] next_gen_14,
  output [15:0] next_gen_15,
  output [15:0] str_right_out,
  output [15:0] next_gen_16,
  output [15:0] next_gen_17,
  output [15:0] next_gen_18,
  output [15:0] next_gen_19,
  output [15:0] next_gen_20,
  output [15:0] next_gen_21,
  output [15:0] next_gen_22,
  output [15:0] next_gen_23,
  output [15:0] next_gen_24,
  output [15:0] next_gen_25,
  output [15:0] next_gen_26,
  output [15:0] next_gen_27,
  output [15:0] next_gen_28,
  output [15:0] next_gen_29,
  output [15:0] next_gen_30,
  output [15:0] next_gen_31,
  output [3:0] corners_out,
  output [15:0] str_left_out
);

  wire undriven_3;
  wire [14:1] str4_t, str5_t, str6_t, str7_t, str8_t, str9_t, str10_t, str11_t, str12_t, str13_t, str14_t,
       str15_t, str16_t, str17_t, str18_t, str19_t, str20_t, str21_t, str22_t, str23_t, str24_t, str25_t,
       str26_t, str27_t, str28_t, str29_t, str30_t;
  wire [15:0] gpu_str_mem_1_pos_next, gpu_str_mem_2_pos_next, gpu_str_mem_3_pos_next, gpu_str_mem_4_pos_next,
       gpu_str_mem_5_pos_next, gpu_str_mem_6_pos_next, gpu_str_mem_7_pos_next, gpu_str_mem_8_pos_next,
       gpu_str_mem_9_pos_next, gpu_str_mem_10_pos_next, gpu_str_mem_11_pos_next, gpu_str_mem_12_pos_next,
       gpu_str_mem_13_pos_next, gpu_str_mem_14_pos_next, gpu_str_mem_15_pos_next, gpu_str_mem_16_pos_next,
       gpu_str_mem_17_pos_next, gpu_str_mem_18_pos_next, gpu_str_mem_19_pos_next, gpu_str_mem_20_pos_next,
       gpu_str_mem_21_pos_next, gpu_str_mem_22_pos_next, gpu_str_mem_23_pos_next, gpu_str_mem_24_pos_next,
       gpu_str_mem_25_pos_next, gpu_str_mem_26_pos_next, gpu_str_mem_27_pos_next, gpu_str_mem_28_pos_next,
       gpu_str_mem_29_pos_next, gpu_str_mem_30_pos_next, gpu_str_mem_31_pos_next, undriven, undriven_2;

  gpu_str_mem gpu_str_mem_1 (
    .data(data), .addr(addr), .str({corners_out[1], str0[14:1], corners_out[0]}), .pos(start_pos),
    .clock(clock), .pos_next(gpu_str_mem_1_pos_next));
  gpu_str_mem gpu_str_mem_2 (
    .data(undriven), .addr(undriven_2), .str({str_down_out[16], str16_t, str_up_out[16]}),
    .clock(undriven_3), .pos_next(gpu_str_mem_2_pos_next));  // open: pos
  gpu_str_mem gpu_str_mem_3 (
    .data(data), .addr(addr), .str(str1), .pos(gpu_str_mem_1_pos_next), .clock(clock),
    .pos_next(gpu_str_mem_3_pos_next));
  gpu_str_mem gpu_str_mem_4 (
    .data(data), .addr(addr), .str(str2), .pos(gpu_str_mem_3_pos_next), .clock(clock),
    .pos_next(gpu_str_mem_4_pos_next));
  gpu_str_mem gpu_str_mem_5 (
    .data(data), .addr(addr), .str(str3), .pos(gpu_str_mem_4_pos_next), .clock(clock),
    .pos_next(gpu_str_mem_5_pos_next));
  gpu_str_mem gpu_str_mem_6 (
    .data(undriven), .addr(undriven_2), .str({str_down_out[17], str17_t, str_up_out[17]}),
    .pos(gpu_str_mem_2_pos_next), .clock(undriven_3), .pos_next(gpu_str_mem_6_pos_next));
  gpu_str_mem gpu_str_mem_7 (
    .data(undriven), .addr(undriven_2), .str({str_down_out[18], str18_t, str_up_out[18]}),
    .pos(gpu_str_mem_6_pos_next), .clock(undriven_3), .pos_next(gpu_str_mem_7_pos_next));
  gpu_str_mem gpu_str_mem_8 (
    .data(data), .addr(addr), .str({str_down_out[4], str4_t, str_up_out[4]}), .pos(gpu_str_mem_5_pos_next),
    .clock(clock), .pos_next(gpu_str_mem_8_pos_next));
  gpu_str_mem gpu_str_mem_9 (
    .data(undriven), .addr(undriven_2), .str({str_down_out[19], str19_t, str_up_out[19]}),
    .pos(gpu_str_mem_7_pos_next), .clock(undriven_3), .pos_next(gpu_str_mem_9_pos_next));
  gpu_str_mem gpu_str_mem_10 (
    .data(data), .addr(addr), .str({str_down_out[5], str5_t, str_up_out[5]}), .pos(gpu_str_mem_8_pos_next),
    .clock(clock), .pos_next(gpu_str_mem_10_pos_next));
  gpu_str_mem gpu_str_mem_11 (
    .data(undriven), .addr(undriven_2), .str({str_down_out[20], str20_t, str_up_out[20]}),
    .pos(gpu_str_mem_9_pos_next), .clock(undriven_3), .pos_next(gpu_str_mem_11_pos_next));
  gpu_str_mem gpu_str_mem_12 (
    .data(data), .addr(addr), .str({str_down_out[6], str6_t, str_up_out[6]}), .pos(gpu_str_mem_10_pos_next),
    .clock(clock), .pos_next(gpu_str_mem_12_pos_next));
  gpu_str_mem gpu_str_mem_13 (
    .data(undriven), .addr(undriven_2), .str({str_down_out[21], str21_t, str_up_out[21]}),
    .pos(gpu_str_mem_11_pos_next), .clock(undriven_3), .pos_next(gpu_str_mem_13_pos_next));
  gpu_str_mem gpu_str_mem_14 (
    .data(data), .addr(addr), .str({str_down_out[7], str7_t, str_up_out[7]}), .pos(gpu_str_mem_12_pos_next),
    .clock(clock), .pos_next(gpu_str_mem_14_pos_next));
  gpu_str_mem gpu_str_mem_15 (
    .data(undriven), .addr(undriven_2), .str({str_down_out[22], str22_t, str_up_out[22]}),
    .pos(gpu_str_mem_13_pos_next), .clock(undriven_3), .pos_next(gpu_str_mem_15_pos_next));
  gpu_str_mem gpu_str_mem_16 (
    .data(data), .addr(addr), .str({str_down_out[8], str8_t, str_up_out[8]}), .pos(gpu_str_mem_14_pos_next),
    .clock(clock), .pos_next(gpu_str_mem_16_pos_next));
  gpu_str_mem gpu_str_mem_17 (
    .data(undriven), .addr(undriven_2), .str({str_down_out[23], str23_t, str_up_out[23]}),
    .pos(gpu_str_mem_15_pos_next), .clock(undriven_3), .pos_next(gpu_str_mem_17_pos_next));
  gpu_str_mem gpu_str_mem_18 (
    .data(data), .addr(addr), .str({str_down_out[9], str9_t, str_up_out[9]}), .pos(gpu_str_mem_16_pos_next),
    .clock(clock), .pos_next(gpu_str_mem_18_pos_next));
  gpu_str_mem gpu_str_mem_19 (
    .data(undriven), .addr(undriven_2), .str({str_down_out[24], str24_t, str_up_out[24]}),
    .pos(gpu_str_mem_17_pos_next), .clock(undriven_3), .pos_next(gpu_str_mem_19_pos_next));
  gpu_str_mem gpu_str_mem_20 (
    .data(data), .addr(addr), .str({str_down_out[10], str10_t, str_up_out[10]}),
    .pos(gpu_str_mem_18_pos_next), .clock(clock), .pos_next(gpu_str_mem_20_pos_next));
  gpu_str_mem gpu_str_mem_21 (
    .data(undriven), .addr(undriven_2), .str({str_down_out[26], str26_t, str_up_out[26]}),
    .pos(gpu_str_mem_22_pos_next), .clock(undriven_3), .pos_next(gpu_str_mem_21_pos_next));
  gpu_str_mem gpu_str_mem_22 (
    .data(undriven), .addr(undriven_2), .str({str_down_out[25], str25_t, str_up_out[25]}),
    .pos(gpu_str_mem_19_pos_next), .clock(undriven_3), .pos_next(gpu_str_mem_22_pos_next));
  gpu_str_mem gpu_str_mem_23 (
    .data(data), .addr(addr), .str({str_down_out[11], str11_t, str_up_out[11]}),
    .pos(gpu_str_mem_20_pos_next), .clock(clock), .pos_next(gpu_str_mem_23_pos_next));
  gpu_str_mem gpu_str_mem_24 (
    .data(undriven), .addr(undriven_2), .str({str_down_out[27], str27_t, str_up_out[27]}),
    .pos(gpu_str_mem_21_pos_next), .clock(undriven_3), .pos_next(gpu_str_mem_24_pos_next));
  gpu_str_mem gpu_str_mem_25 (
    .data(data), .addr(addr), .str({str_down_out[12], str12_t, str_up_out[12]}),
    .pos(gpu_str_mem_23_pos_next), .clock(clock), .pos_next(gpu_str_mem_25_pos_next));
  gpu_str_mem gpu_str_mem_26 (
    .data(undriven), .addr(undriven_2), .str({str_down_out[28], str28_t, str_up_out[28]}),
    .pos(gpu_str_mem_24_pos_next), .clock(undriven_3), .pos_next(gpu_str_mem_26_pos_next));
  gpu_str_mem gpu_str_mem_27 (
    .data(data), .addr(addr), .str({str_down_out[13], str13_t, str_up_out[13]}),
    .pos(gpu_str_mem_25_pos_next), .clock(clock), .pos_next(gpu_str_mem_27_pos_next));
  gpu_str_mem gpu_str_mem_28 (
    .data(undriven), .addr(undriven_2), .str({str_down_out[29], str29_t, str_up_out[29]}),
    .pos(gpu_str_mem_26_pos_next), .clock(undriven_3), .pos_next(gpu_str_mem_28_pos_next));
  gpu_str_mem gpu_str_mem_29 (
    .data(data), .addr(addr), .str({str_down_out[14], str14_t, str_up_out[14]}),
    .pos(gpu_str_mem_27_pos_next), .clock(clock), .pos_next(gpu_str_mem_29_pos_next));
  gpu_str_mem gpu_str_mem_30 (
    .data(undriven), .addr(undriven_2), .str({str_down_out[30], str30_t, str_up_out[30]}),
    .pos(gpu_str_mem_28_pos_next), .clock(undriven_3), .pos_next(gpu_str_mem_30_pos_next));
  gpu_str_mem gpu_str_mem_31 (
    .data(data), .addr(addr), .str({str_down_out[15], str15_t, str_up_out[15]}),
    .pos(gpu_str_mem_29_pos_next), .clock(clock), .pos_next(gpu_str_mem_31_pos_next));
  gpu_str_mem gpu_str_mem_32 (
    .data(undriven), .addr(undriven_2), .str({corners_out[2], str_right_out[14:1], corners_out[3]}),
    .pos(gpu_str_mem_30_pos_next), .clock(undriven_3));  // open: pos_next

  assign {str0[15], str0[0]} = corners_out[1:0];
  assign {str_down_out[31], str_down_out[3:0]} = {corners_out[2], str3[15], str2[15], str1[15], corners_out[1]};
  assign str_left_out = str1;
  assign {str_right_out[15], str_right_out[0]} = {corners_out[2], corners_out[3]};
  assign {str_up_out[31], str_up_out[3:0]} = {corners_out[3], str3[0], str2[0], str1[0], corners_out[0]};

  // Other names for the same wires on the sheet: down0 = corners_out[1]; down31 = corners_out[2];
  //   str31_t[15:0] = {corners_out[2], str_right_out[14:1], corners_out[3]}; ng0[15:0] = next_gen_0;
  //   ng1[15:0] = next_gen_1; ng2[15:0] = next_gen_2; ng3[15:0] = next_gen_3; ng4[15:0] = next_gen_4;
  //   ng5[15:0] = next_gen_5; ng6[15:0] = next_gen_6; ng7[15:0] = next_gen_7; ng8[15:0] = next_gen_8;
  //   ng9[15:0] = next_gen_9; ng10[15:0] = next_gen_10; ng11[15:0] = next_gen_11; ng12[15:0] = next_gen_12;
  //   ng13[15:0] = next_gen_13; ng14[15:0] = next_gen_14; ng15[15:0] = next_gen_15; ng16[15:0] = next_gen_16;
  //   ng17[15:0] = next_gen_17; ng18[15:0] = next_gen_18; ng19[15:0] = next_gen_19; ng20[15:0] = next_gen_20;
  //   ng21[15:0] = next_gen_21; ng22[15:0] = next_gen_22; ng23[15:0] = next_gen_23; ng24[15:0] = next_gen_24;
  //   ng25[15:0] = next_gen_25; ng26[15:0] = next_gen_26; ng27[15:0] = next_gen_27; ng28[15:0] = next_gen_28;
  //   ng29[15:0] = next_gen_29; ng30[15:0] = next_gen_30; ng31[15:0] = next_gen_31; down1 = str1[15];
  //   down2 = str2[15]; down3 = str3[15]; down4 = str_down_out[4];
  //   str4_t (some bits) = {str_down_out[4], str_up_out[4]}; down5 = str_down_out[5];
  //   str5_t (some bits) = {str_down_out[5], str_up_out[5]}; down6 = str_down_out[6];
  //   str6_t (some bits) = {str_down_out[6], str_up_out[6]}; down7 = str_down_out[7];
  //   str7_t (some bits) = {str_down_out[7], str_up_out[7]}; down8 = str_down_out[8];
  //   str8_t (some bits) = {str_down_out[8], str_up_out[8]}; down9 = str_down_out[9];
  //   str9_t (some bits) = {str_down_out[9], str_up_out[9]}; down10 = str_down_out[10];
  //   str10_t (some bits) = {str_down_out[10], str_up_out[10]}; down11 = str_down_out[11];
  //   str11_t (some bits) = {str_down_out[11], str_up_out[11]}; down12 = str_down_out[12];
  //   str12_t (some bits) = {str_down_out[12], str_up_out[12]}; down13 = str_down_out[13];
  //   str13_t (some bits) = {str_down_out[13], str_up_out[13]}; down14 = str_down_out[14];
  //   str14_t (some bits) = {str_down_out[14], str_up_out[14]}; down15 = str_down_out[15];
  //   str15_t (some bits) = {str_down_out[15], str_up_out[15]}; down16 = str_down_out[16];
  //   str16_t (some bits) = {str_down_out[16], str_up_out[16]}; down17 = str_down_out[17];
  //   str17_t (some bits) = {str_down_out[17], str_up_out[17]}; down18 = str_down_out[18];
  //   str18_t (some bits) = {str_down_out[18], str_up_out[18]}; down19 = str_down_out[19];
  //   str19_t (some bits) = {str_down_out[19], str_up_out[19]}; down20 = str_down_out[20];
  //   str20_t (some bits) = {str_down_out[20], str_up_out[20]}; down21 = str_down_out[21];
  //   str21_t (some bits) = {str_down_out[21], str_up_out[21]}; down22 = str_down_out[22];
  //   str22_t (some bits) = {str_down_out[22], str_up_out[22]}; down23 = str_down_out[23];
  //   str23_t (some bits) = {str_down_out[23], str_up_out[23]}; down24 = str_down_out[24];
  //   str24_t (some bits) = {str_down_out[24], str_up_out[24]}; down25 = str_down_out[25];
  //   str25_t (some bits) = {str_down_out[25], str_up_out[25]}; down26 = str_down_out[26];
  //   str26_t (some bits) = {str_down_out[26], str_up_out[26]}; down27 = str_down_out[27];
  //   str27_t (some bits) = {str_down_out[27], str_up_out[27]}; down28 = str_down_out[28];
  //   str28_t (some bits) = {str_down_out[28], str_up_out[28]}; down29 = str_down_out[29];
  //   str29_t (some bits) = {str_down_out[29], str_up_out[29]}; down30 = str_down_out[30];
  //   str30_t (some bits) = {str_down_out[30], str_up_out[30]}; up0 = corners_out[0]; up1 = str1[0]; up2 = str2[0];
  //   up3 = str3[0]; up4 = str_up_out[4]; up5 = str_up_out[5]; up6 = str_up_out[6]; up7 = str_up_out[7];
  //   up8 = str_up_out[8]; up9 = str_up_out[9]; up10 = str_up_out[10]; up11 = str_up_out[11]; up12 = str_up_out[12];
  //   up13 = str_up_out[13]; up14 = str_up_out[14]; up15 = str_up_out[15]; up16 = str_up_out[16];
  //   up17 = str_up_out[17]; up18 = str_up_out[18]; up19 = str_up_out[19]; up20 = str_up_out[20];
  //   up21 = str_up_out[21]; up22 = str_up_out[22]; up23 = str_up_out[23]; up24 = str_up_out[24];
  //   up25 = str_up_out[25]; up26 = str_up_out[26]; up27 = str_up_out[27]; up28 = str_up_out[28];
  //   up29 = str_up_out[29]; up30 = str_up_out[30]; up31 = corners_out[3]

  // Notes on the sheet:
  //   *ВСТАВЬТЕ ВИДЕОКАРТУ ИЛИ УДАЛИТЕ*
endmodule

// button controller
module but_control (
  input  clock,
  input  read,
  input  [15:0] addr,
  input  IAck,
  input  life_on,
  input  down,
  input  life_off,
  input  set_op,
  input  reset_all,
  input  left,
  input  up,
  input  right,
  output IRQ,
  output [15:0] data,
  output [5:0] vec
);

  wire comparator_1_eq, counter_1_carry, counter_2_carry, counter_3_carry, counter_4_carry, counter_5_carry,
       counter_6_carry, counter_7_carry, counter_8_carry, down_t, got, not_1_out, not_2_out, not_3_out,
       not_4_out, not_5_out, not_6_out, not_7_out, not_8_out, or_1_out;
  wire [7:0] flag;
  wire [15:0] register_1_q;

  D_Flip_Flop d_ff_1 (.clk(life_on), .D(1'b1), .Q(flag[0]), .reset(counter_1_carry));  // open: Qn, preset, en
  Counter #(.width(4), .max('hf)) counter_1 (
    .count(flag[0]), .carry(counter_1_carry), .clk(clock), .clr(not_1_out));  // open: load, D, Q
  not not_1 (not_1_out, flag[0]);
  D_Flip_Flop d_ff_2 (.clk(life_off), .D(1'b1), .Q(flag[1]), .reset(counter_2_carry));  // open: Qn, preset, en
  Counter #(.width(4), .max('hf)) counter_2 (
    .count(flag[1]), .carry(counter_2_carry), .clk(clock), .clr(not_2_out));  // open: load, D, Q
  not not_2 (not_2_out, flag[1]);
  D_Flip_Flop d_ff_3 (.clk(reset_all), .D(1'b1), .Q(flag[2]), .reset(counter_3_carry));  // open: Qn, preset, en
  Counter #(.width(4), .max('hf)) counter_3 (
    .count(flag[2]), .carry(counter_3_carry), .clk(clock), .clr(not_3_out));  // open: load, D, Q
  not not_3 (not_3_out, flag[2]);
  D_Flip_Flop d_ff_4 (.clk(up), .D(1'b1), .Q(flag[3]), .reset(counter_4_carry));  // open: Qn, preset, en
  Counter #(.width(4), .max('hf)) counter_4 (
    .count(flag[3]), .carry(counter_4_carry), .clk(clock), .clr(not_4_out));  // open: load, D, Q
  not not_4 (not_4_out, flag[3]);
  Counter #(.width(4), .max('hf)) counter_5 (
    .count(down_t), .carry(counter_5_carry), .clk(clock), .clr(not_5_out));  // open: load, D, Q
  not not_5 (not_5_out, down_t);
  Counter #(.width(4), .max('hf)) counter_6 (
    .count(flag[7]), .carry(counter_6_carry), .clk(clock), .clr(not_6_out));  // open: load, D, Q
  not not_6 (not_6_out, flag[7]);
  Counter #(.width(4), .max('hf)) counter_7 (
    .count(flag[5]), .carry(counter_7_carry), .clk(clock), .clr(not_7_out));  // open: load, D, Q
  not not_7 (not_7_out, flag[5]);
  Counter #(.width(4), .max('hf)) counter_8 (
    .count(flag[4]), .carry(counter_8_carry), .clk(clock), .clr(not_8_out));  // open: load, D, Q
  not not_8 (not_8_out, flag[4]);
  D_Flip_Flop d_ff_5 (.clk(down), .D(1'b1), .Q(down_t), .reset(counter_5_carry));  // open: Qn, preset, en
  D_Flip_Flop d_ff_6 (.clk(set_op), .D(1'b1), .Q(flag[7]), .reset(counter_6_carry));  // open: Qn, preset, en
  D_Flip_Flop d_ff_7 (.clk(left), .D(1'b1), .Q(flag[5]), .reset(counter_7_carry));  // open: Qn, preset, en
  D_Flip_Flop d_ff_8 (.clk(right), .D(1'b1), .Q(flag[4]), .reset(counter_8_carry));  // open: Qn, preset, en
  Register #(.width(16)) register_1 (
    .D({{8{1'b0}}, flag[7], down_t, flag[5:0]}), .Q(register_1_q), .clk(IRQ));  // open: en, clr
  assign data = got ? register_1_q : 16'bz;  // Controlled_Buffer controlled_buffer_1
  Multiplexer #(.width(6), .enable("false")) multiplexer_1 (
    .in0(6'b000101), .in1(6'b000110), .out(vec), .sel(or_1_out));
  or or_1 (or_1_out, flag[0], flag[1]);
  or or_2 (IRQ, flag[0], flag[1], flag[2], flag[3], flag[4], flag[5], down_t, flag[7], 1'b0, 1'b0, 1'b0, 1'b0, 1'b0, 1'b0, 1'b0, 1'b0);
  and and_1 (got, read, comparator_1_eq);
  Comparator #(.width(16)) comparator_1 (.a(addr), .b(16'hfff0), .eq(comparator_1_eq));  // open: gt, lt

  // Other names for the same wires on the sheet: life_on_t = flag[0]; life_off_t = flag[1]; reset_all_t = flag[2];
  //   up_t = flag[3]; right_t = flag[4]; left_t = flag[5]; flag[6] = down_t; set_op_t = flag[7]

  // Notes on the sheet:
  //   data: pull=down
  //   addr: pull=down
  //   set_handler
  //   life_handler
endmodule
